# Fritzing sketch prototype (saved by Fritzing 0.9.3b)
breadboards: 1

parts:
  Part1 = Arduino Uno (Rev3) - ICSP
  U1 = POT [package=pot_alpha_rv16af-20]
  LED1 = smd LED [color="Red (633nm)" package="1206 [SMD]"]

nets:
  N1: Part1.A0, U1.S
  N2: Part1.D9_PWM, LED1.anode
  N3: Part1.5V, U1.E
  N4: Part1.GND, U1.A, LED1.cathode
